// Digital circuit ALU - Circuit.dig as structural Verilog
module ALU___Circuit (
  input  b_0,
  input  a_0,
  input  op_1,
  input  op_2,
  input  op_3,
  input  op_0,
  input  b_1,
  input  a_1,
  input  b_2,
  input  a_2,
  input  b_3,
  input  a_3,
  output r_0,
  output r_1,
  output r_2,
  output r_3,
  output c_out
);

  wire [0:0] rom_1_d, rom_3_d, rom_5_d;

  ROM #(.AddrBits(7)) rom_1 (.A({op_0, op_1, op_2, op_3, a_0, b_0, 1'b0}), .sel(1'b1), .D(rom_1_d[0]));
  ROM #(.AddrBits(8)) rom_2 (.A({op_0, op_1, op_2, op_3, a_0, b_0, 2'b00}), .sel(1'b1), .D(r_0));
  ROM #(.AddrBits(7)) rom_3 (.A({op_0, op_1, op_2, op_3, a_1, b_1, rom_1_d[0]}), .sel(1'b1), .D(rom_3_d[0]));
  ROM #(.AddrBits(8)) rom_4 (.A({op_0, op_1, op_2, op_3, a_1, b_1, rom_1_d[0], a_0}), .sel(1'b1), .D(r_1));
  ROM #(.AddrBits(7)) rom_5 (.A({op_0, op_1, op_2, op_3, a_2, b_2, rom_3_d[0]}), .sel(1'b1), .D(rom_5_d[0]));
  ROM #(.AddrBits(8)) rom_6 (.A({op_0, op_1, op_2, op_3, a_2, b_2, rom_3_d[0], a_1}), .sel(1'b1), .D(r_2));
  ROM #(.AddrBits(7)) rom_7 (.A({op_0, op_1, op_2, op_3, a_3, b_3, rom_5_d[0]}), .sel(1'b1), .D(c_out));
  ROM #(.AddrBits(8)) rom_8 (.A({op_0, op_1, op_2, op_3, a_3, b_3, rom_5_d[0], a_2}), .sel(1'b1), .D(r_3));

  // Notes on the sheet:
  //   contents of rom_1 (hex, n*v repeats v):
  //   0,0,0,1,0,1,1,1,4*0,4*1
  //   contents of rom_2 (hex, n*v repeats v):
  //   0,0,4*1,0,0,1,1,4*0,1,1,0,1,0,1,0,1,0,1,0,1,0,1,0,1,0,1,12*0,1,1
  //   ,22*0,1,1,0,0,1,1,0,0,1,1,22*0,1,1,0,0,1,1,22*0,1,1,10*0,1,1,18*0
  //   ,1,1,0,0,1,1,0,0,1,1,22*0,1,1,30*0,1,1,0,0,1,1
  //   contents of rom_3 (hex, n*v repeats v):
  //   0,0,0,1,0,1,1,1,4*0,4*1
  //   contents of rom_4 (hex, n*v repeats v):
  //   0,0,4*1,0,0,1,1,4*0,1,1,0,1,0,1,0,1,0,1,0,1,0,1,0,1,0,1,12*0,1,1
  //   ,22*0,1,1,0,0,1,1,0,0,1,1,22*0,1,1,0,0,1,1,22*0,1,1,10*0,1,1,18*0
  //   ,1,1,0,0,1,1,0,0,1,1,22*0,1,1,30*0,1,1,0,0,1,1
  //   contents of rom_5 (hex, n*v repeats v):
  //   0,0,0,1,0,1,1,1,4*0,4*1
  //   contents of rom_6 (hex, n*v repeats v):
  //   0,0,4*1,0,0,1,1,4*0,1,1,0,1,0,1,0,1,0,1,0,1,0,1,0,1,0,1,12*0,1,1
  //   ,22*0,1,1,0,0,1,1,0,0,1,1,22*0,1,1,0,0,1,1,22*0,1,1,10*0,1,1,18*0
  //   ,1,1,0,0,1,1,0,0,1,1,22*0,1,1,30*0,1,1,0,0,1,1
  //   contents of rom_7 (hex, n*v repeats v):
  //   0,0,0,1,0,1,1,1,4*0,4*1
  //   contents of rom_8 (hex, n*v repeats v):
  //   0,0,4*1,0,0,1,1,4*0,1,1,0,1,0,1,0,1,0,1,0,1,0,1,0,1,0,1,12*0,1,1
  //   ,22*0,1,1,0,0,1,1,0,0,1,1,22*0,1,1,0,0,1,1,22*0,1,1,10*0,1,1,18*0
  //   ,1,1,0,0,1,1,0,0,1,1,22*0,1,1,30*0,1,1,0,0,1,1
endmodule
