// Digital circuit Elevetor - Circuit.dig as structural Verilog
module Elevetor___Circuit (
  input  P_3,
  input  P_2,
  input  P_1,
  input  P_0,
  input  P_VIP,
  input  A_VIP,
  input  A_3,
  input  A_2,
  input  A_1,
  input  A_0,
  input  CK,
  output y_2,
  output y_1,
  output y_0,
  output z_2,
  output z_1,
  output z_0,
  output out_18
);

  wire and_2_out, and_3_out, and_4_out, and_5_out, and_8_out, and_10_out, and_11_out, and_12_out,
       comparator_15_eq, comparator_16_eq, comparator_17_eq, comparator_18_eq, comparator_19_eq, d_ff_1_q,
       d_ff_2_q, d_ff_3_q, d_ff_4_q, d_ff_5_q, d_ff_6_q, d_ff_7_q, d_ff_8_q, delay_1_out, EN_1, EN_2, EN_3,
       \new , or_6_out, or_7_out, or_8_out, or_9_out, or_10_out, or_11_out, or_12_out, or_14_out, or_15_out,
       P_0c, P_1c, P_2c, P_3c, P_Vipc, R_1_eq_0, R_1_eq_VIP, R_2_eq_0, R_2_eq_VIP, R_2_gt_R_1, R_3_eq_0,
       R_3_eq_VIP, R_3_gt_R_2, R_4_eq_0, R_4_eq_VIP, R_4_gt_R_3, R_5_eq_0, R_5_eq_VIP, R_5_gt_R_4, xor_1_out,
       y_01, y_11, y_21, Y_gt_R_1, Y_gt_R_2, Y_gt_R_3, Y_gt_R_4, Y_gt_R_5;
  wire [1:0] delay_2_out, delay_3_out, delay_4_out, delay_5_out, delay_6_out, multiplexer_1_out,
       multiplexer_2_out, multiplexer_3_out, multiplexer_4_out, multiplexer_5_out, multiplexer_6_out,
       multiplexer_7_out, multiplexer_8_out, or_13_out, rom_8_d, rom_8_d_2, rom_9_d, rom_9_d_2, rom_10_d,
       rom_10_d_2, rom_11_d, rom_11_d_2;
  wire [2:0] rom_1_d, rom_12_d;
  wire [4:0] multiplexer_9_out, multiplexer_10_out, multiplexer_11_out, multiplexer_12_out,
       multiplexer_13_out, or_1_out, or_2_out, or_3_out, or_4_out, or_5_out, Reg_1, Reg_2, Reg_3, Reg_4,
       Reg_5, Registro_1_d, Registro_2_d, Registro_3_d, Registro_4_d, W, Y_5;
  wire [6:6] and_1_out;

  ROM #(.AddrBits(5), .Bits(3)) rom_1 (.A({R_1_eq_0, R_2_eq_0, R_3_eq_0, R_4_eq_0, R_5_eq_0}), .sel(1'b1), .D(rom_1_d));
  ROM #(.AddrBits(6)) rom_2 (.A({Reg_5[0], Reg_4[0], Reg_3[0], Reg_2[0], Reg_1[0], P_0}), .sel(1'b1), .D(P_0c));
  ROM #(.AddrBits(6)) rom_3 (.A({Reg_5[1], Reg_4[1], Reg_3[1], Reg_2[1], Reg_1[1], P_1}), .sel(1'b1), .D(P_1c));
  ROM #(.AddrBits(6)) rom_4 (.A({Reg_5[2], Reg_4[2], Reg_3[2], Reg_2[2], Reg_1[2], P_2}), .sel(1'b1), .D(P_2c));
  ROM #(.AddrBits(6)) rom_5 (.A({Reg_5[3], Reg_4[3], Reg_3[3], Reg_2[3], Reg_1[3], P_3}), .sel(1'b1), .D(P_3c));
  ROM #(.AddrBits(6)) rom_6 (.A({Reg_5[4], Reg_4[4], Reg_3[4], Reg_2[4], Reg_1[4], P_VIP}), .sel(1'b1), .D(P_Vipc));
  and and_1 (and_1_out[6], ~z_2, z_1, z_0);  // And
  ROM #(.AddrBits(3), .Bits(5)) rom_7 (.A({y_2, y_1, y_0}), .sel(1'b1), .D(Y_5));
  ROM #(.AddrBits(8), .Bits(5)) Registro_1 (
    .A({P_0c, P_1c, P_2c, P_3c, P_Vipc, rom_1_d}), .sel(1'b1), .D(Registro_1_d));
  ROM #(.AddrBits(8), .Bits(5)) Registro_2 (
    .A({P_0c, P_1c, P_2c, P_3c, P_Vipc, rom_1_d}), .sel(1'b1), .D(Registro_2_d));
  ROM #(.AddrBits(8), .Bits(5)) Registro_3 (
    .A({P_0c, P_1c, P_2c, P_3c, P_Vipc, rom_1_d}), .sel(1'b1), .D(Registro_3_d));
  ROM #(.AddrBits(8), .Bits(5)) Registro_4 (
    .A({P_0c, P_1c, P_2c, P_3c, P_Vipc, rom_1_d}), .sel(1'b1), .D(Registro_4_d));
  ROM #(.AddrBits(8), .Bits(5)) Registro_5 (.A({P_0c, P_1c, P_2c, P_3c, P_Vipc, rom_1_d}), .sel(1'b1), .D(W));
  Comparator #(.Bits(5)) comparator_1 (.a(Y_5), .b(Reg_1), .gt(Y_gt_R_1));  // open: eq, lt
  Comparator #(.Bits(5)) comparator_2 (.a(Y_5), .b(Reg_2), .gt(Y_gt_R_2));  // open: eq, lt
  Comparator #(.Bits(5)) comparator_3 (.a(Y_5), .b(Reg_3), .gt(Y_gt_R_3));  // open: eq, lt
  Comparator #(.Bits(5)) comparator_4 (.a(Y_5), .b(Reg_4), .gt(Y_gt_R_4));  // open: eq, lt
  Comparator #(.Bits(5)) comparator_5 (.a(Y_5), .b(Reg_5), .gt(Y_gt_R_5));  // open: eq, lt
  Comparator #(.Bits(5)) comparator_6 (.a(Reg_2), .b(Reg_1), .gt(R_2_gt_R_1));  // open: eq, lt
  Comparator #(.Bits(5)) comparator_7 (.a(Reg_3), .b(Reg_2), .gt(R_3_gt_R_2));  // open: eq, lt
  Comparator #(.Bits(5)) comparator_8 (.a(Reg_4), .b(Reg_3), .gt(R_4_gt_R_3));  // open: eq, lt
  Comparator #(.Bits(5)) comparator_9 (.a(Reg_5), .b(Reg_4), .gt(R_5_gt_R_4));  // open: eq, lt
  Comparator #(.Bits(5)) comparator_10 (.a(Reg_1), .b(5'b10000), .eq(R_1_eq_VIP));  // open: gt, lt
  Comparator #(.Bits(5)) comparator_11 (.a(Reg_2), .b(5'b10000), .eq(R_2_eq_VIP));  // open: gt, lt
  Comparator #(.Bits(5)) comparator_12 (.a(Reg_3), .b(5'b10000), .eq(R_3_eq_VIP));  // open: gt, lt
  Comparator #(.Bits(5)) comparator_13 (.a(Reg_4), .b(5'b10000), .eq(R_4_eq_VIP));  // open: gt, lt
  Comparator #(.Bits(5)) comparator_14 (.a(Reg_5), .b(5'b10000), .eq(R_5_eq_VIP));  // open: gt, lt
  assign or_1_out = Reg_1 | Registro_1_d;  // Or or_1, 5 bits wide
  assign or_2_out = Reg_2 | Registro_2_d;  // Or or_2, 5 bits wide
  assign or_3_out = Reg_3 | Registro_3_d;  // Or or_3, 5 bits wide
  assign or_4_out = Reg_4 | Registro_4_d;  // Or or_4, 5 bits wide
  assign or_5_out = Reg_5 | W;  // Or or_5, 5 bits wide
  and and_2 (and_2_out, ~z_2, z_1, z_0);  // And
  Comparator #(.Bits(5)) comparator_15 (.a({5{1'b0}}), .b(W), .eq(comparator_15_eq));  // open: gt, lt
  Comparator #(.Bits(5)) comparator_16 (.a({5{1'b0}}), .b(Registro_4_d), .eq(comparator_16_eq));  // open: gt, lt
  Comparator #(.Bits(5)) comparator_17 (.a({5{1'b0}}), .b(Registro_3_d), .eq(comparator_17_eq));  // open: gt, lt
  Comparator #(.Bits(5)) comparator_18 (.a({5{1'b0}}), .b(Registro_2_d), .eq(comparator_18_eq));  // open: gt, lt
  Comparator #(.Bits(5)) comparator_19 (.a({5{1'b0}}), .b(Registro_1_d), .eq(comparator_19_eq));  // open: gt, lt
  ROM #(.AddrBits(7), .Bits(4)) rom_8 (
    .A({and_1_out[6], R_1_eq_VIP, \new , Y_gt_R_1, Y_gt_R_2, R_2_gt_R_1, R_2_eq_VIP}), .sel(1'b1),
    .D({rom_8_d_2, rom_8_d}));
  ROM #(.AddrBits(7), .Bits(4)) rom_9 (
    .A({R_2_eq_VIP, \new , Y_gt_R_1, Y_gt_R_2, Y_gt_R_3, R_3_gt_R_2, R_3_eq_VIP}), .sel(1'b1),
    .D({rom_9_d_2, rom_9_d}));
  ROM #(.AddrBits(7), .Bits(4)) rom_10 (
    .A({R_3_eq_VIP, \new , Y_gt_R_1, Y_gt_R_3, Y_gt_R_4, R_4_gt_R_3, R_4_eq_VIP}), .sel(1'b1),
    .D({rom_10_d_2, rom_10_d}));
  ROM #(.AddrBits(7), .Bits(4)) rom_11 (
    .A({R_4_eq_VIP, \new , Y_gt_R_1, Y_gt_R_4, Y_gt_R_5, R_5_gt_R_4, R_5_eq_VIP}), .sel(1'b1),
    .D({rom_11_d_2, rom_11_d}));
  D_FF d_ff_1 (.D(and_2_out), .C(CK), .Q(d_ff_1_q));  // open: nQ
  or or_6 (or_6_out, ~comparator_15_eq, ~comparator_16_eq, ~comparator_17_eq, ~comparator_18_eq, ~comparator_19_eq);  // Or
  and and_3 (and_3_out, d_ff_1_q, and_2_out);
  Delay delay_1 (.in(or_6_out), .out(delay_1_out));
  or or_7 (or_7_out, rom_9_d_2[0], rom_9_d_2[1]);
  or or_8 (or_8_out, rom_10_d_2[0], rom_10_d_2[1]);
  or or_9 (or_9_out, rom_11_d_2[0], rom_11_d_2[1]);
  D_FF d_ff_2 (.D(and_3_out), .C(CK), .Q(d_ff_2_q));  // open: nQ
  and and_4 (and_4_out, d_ff_2_q, and_2_out);
  Multiplexer #(.Bits(2)) multiplexer_1 (.sel(or_7_out), .in_0(rom_8_d), .in_1(rom_9_d_2), .out(multiplexer_1_out));
  Multiplexer #(.Bits(2)) multiplexer_2 (.sel(or_8_out), .in_0(rom_9_d), .in_1(rom_10_d_2), .out(multiplexer_2_out));
  Multiplexer #(.Bits(2)) multiplexer_3 (.sel(or_9_out), .in_0(rom_10_d), .in_1(rom_11_d_2), .out(multiplexer_3_out));
  Comparator #(.Bits(5)) comparator_20 (.a(Reg_1), .b({5{1'b0}}), .eq(R_1_eq_0));  // open: gt, lt
  Comparator #(.Bits(5)) comparator_21 (.a(Reg_2), .b({5{1'b0}}), .eq(R_2_eq_0));  // open: gt, lt
  Comparator #(.Bits(5)) comparator_22 (.a(Reg_3), .b({5{1'b0}}), .eq(R_3_eq_0));  // open: gt, lt
  Comparator #(.Bits(5)) comparator_23 (.a(Reg_4), .b({5{1'b0}}), .eq(R_4_eq_0));  // open: gt, lt
  Comparator #(.Bits(5)) comparator_24 (.a(Reg_5), .b({5{1'b0}}), .eq(R_5_eq_0));  // open: gt, lt
  D_FF d_ff_3 (.D(and_4_out), .C(CK), .Q(d_ff_3_q));  // open: nQ
  Multiplexer #(.Bits(2)) multiplexer_4 (.sel(EN_1), .in_0(rom_8_d_2), .in_1(2'b00), .out(multiplexer_4_out));
  Multiplexer #(.Bits(2)) multiplexer_5 (.sel(EN_2), .in_0(multiplexer_1_out), .in_1(2'b00), .out(multiplexer_5_out));
  Multiplexer #(.Bits(2)) multiplexer_6 (.sel(EN_3), .in_0(multiplexer_2_out), .in_1(2'b00), .out(multiplexer_6_out));
  and and_5 (and_5_out, d_ff_3_q, and_2_out);
  or or_10 (or_10_out, multiplexer_3_out[0], multiplexer_3_out[1], EN_3);
  or or_11 (or_11_out, rom_11_d[0], rom_11_d[1]);
  Multiplexer #(.Bits(2)) multiplexer_7 (.sel(1'b0), .in_0(multiplexer_4_out), .in_1(2'b00), .out(multiplexer_7_out));
  and and_6 (EN_2, or_10_out, ~\new );  // And
  D_FF d_ff_4 (.D(and_5_out), .C(CK), .Q(d_ff_4_q));  // open: nQ
  or or_12 (or_12_out, multiplexer_6_out[0], multiplexer_6_out[1], EN_2);
  and and_7 (EN_3, or_11_out, ~\new );  // And
  and and_8 (and_8_out, d_ff_4_q, and_2_out);
  and and_9 (EN_1, or_12_out, ~\new );  // And
  Multiplexer #(.Bits(2)) multiplexer_8 (.sel(1'b0), .in_0(multiplexer_3_out), .in_1(2'b00), .out(multiplexer_8_out));
  ROM #(.AddrBits(12), .Bits(4)) rom_12 (
    .A({out_18, y_21, y_11, y_01, Reg_1, z_2, z_1, z_0}), .sel(1'b1), .D({\new , rom_12_d}));
  D_FF d_ff_5 (.D(and_8_out), .C(CK), .Q(d_ff_5_q));  // open: nQ
  Multiplexer #(.Selector_Bits(2), .Bits(5)) multiplexer_9 (
    .sel(multiplexer_7_out), .in_0(or_1_out), .in_1({5{1'b0}}), .in_2(Reg_2), .in_3({5{1'b0}}),
    .out(multiplexer_9_out));
  Delay #(.Bits(2)) delay_2 (.in(multiplexer_7_out), .out(delay_2_out));
  Multiplexer #(.Selector_Bits(2), .Bits(5)) multiplexer_10 (
    .sel(multiplexer_5_out), .in_0(or_2_out), .in_1(Reg_1), .in_2(Reg_3), .in_3({5{1'b0}}),
    .out(multiplexer_10_out));
  Multiplexer #(.Selector_Bits(2), .Bits(5)) multiplexer_11 (
    .sel(multiplexer_6_out), .in_0(or_3_out), .in_1(Reg_2), .in_2(Reg_4), .in_3({5{1'b0}}),
    .out(multiplexer_11_out));
  Multiplexer #(.Selector_Bits(2), .Bits(5)) multiplexer_12 (
    .sel(multiplexer_8_out), .in_0(or_4_out), .in_1(Reg_3), .in_2(Reg_5), .in_3({5{1'b0}}),
    .out(multiplexer_12_out));
  Multiplexer #(.Selector_Bits(2), .Bits(5)) multiplexer_13 (
    .sel(rom_11_d), .in_0(or_5_out), .in_1(Reg_4), .in_2({5{1'b0}}), .in_3({5{1'b0}}),
    .out(multiplexer_13_out));
  and and_10 (and_10_out, d_ff_5_q, and_2_out);
  Delay #(.Bits(2)) delay_3 (.in(multiplexer_5_out), .out(delay_3_out));
  Delay #(.Bits(2)) delay_4 (.in(multiplexer_6_out), .out(delay_4_out));
  Delay #(.Bits(2)) delay_5 (.in(multiplexer_8_out), .out(delay_5_out));
  Delay #(.Bits(2)) delay_6 (.in(rom_11_d), .out(delay_6_out));
  D_FF d_ff_6 (.D(and_10_out), .C(CK), .Q(d_ff_6_q));  // open: nQ
  ROM #(.AddrBits(8)) rom_13 (.A({A_VIP, A_3, A_2, A_1, A_0, y_2, y_1, y_0}), .sel(1'b1), .D(y_21));
  ROM #(.AddrBits(8)) rom_14 (.A({A_VIP, A_3, A_2, A_1, A_0, y_2, y_1, y_0}), .sel(1'b1), .D(y_11));
  ROM #(.AddrBits(8)) rom_15 (.A({A_VIP, A_3, A_2, A_1, A_0, y_2, y_1, y_0}), .sel(1'b1), .D(y_01));
  and and_11 (and_11_out, d_ff_6_q, and_2_out);
  assign or_13_out = delay_2_out | delay_3_out | delay_4_out | delay_5_out | delay_6_out;  // Or or_13, 2 bits wide
  Register #(.Bits(5)) R_1 (.D(multiplexer_9_out), .C(xor_1_out), .en(1'b1), .Q(Reg_1));
  Register #(.Bits(5)) R_2 (.D(multiplexer_10_out), .C(xor_1_out), .en(1'b1), .Q(Reg_2));
  Register #(.Bits(5)) R_3 (.D(multiplexer_11_out), .C(xor_1_out), .en(1'b1), .Q(Reg_3));
  Register #(.Bits(5)) R_4 (.D(multiplexer_12_out), .C(xor_1_out), .en(1'b1), .Q(Reg_4));
  Register #(.Bits(5)) R_5 (.D(multiplexer_13_out), .C(xor_1_out), .en(1'b1), .Q(Reg_5));
  D_FF d_ff_7 (.D(and_11_out), .C(CK), .Q(d_ff_7_q));  // open: nQ
  or or_14 (or_14_out, or_13_out[0], or_13_out[1]);
  and and_12 (and_12_out, d_ff_7_q, and_2_out);
  or or_15 (or_15_out, delay_1_out, or_14_out);
  D_FF Y_2_n (.D(y_21), .C(CK), .Q(y_2));  // open: nQ
  D_FF Y_1_n (.D(y_11), .C(CK), .Q(y_1));  // open: nQ
  D_FF Y_0_n (.D(y_01), .C(CK), .Q(y_0));  // open: nQ
  D_FF Z_2_n (.D(rom_12_d[2]), .C(CK), .Q(z_2));  // open: nQ
  D_FF Z_1_n (.D(rom_12_d[1]), .C(CK), .Q(z_1));  // open: nQ
  D_FF Z_0_n (.D(rom_12_d[0]), .C(CK), .Q(z_0));  // open: nQ
  D_FF d_ff_8 (.D(and_12_out), .C(CK), .Q(d_ff_8_q));  // open: nQ
  and and_13 (out_18, d_ff_8_q, and_2_out);
  xor xor_1 (xor_1_out, CK, or_15_out);

  // Other names for the same wires on the sheet: Reg_1_0 = Reg_1[0]; Reg_1_1 = Reg_1[1]; Reg_1_2 = Reg_1[2];
  //   Reg_1_3 = Reg_1[3]; Reg_1_4 = Reg_1[4]; Reg_2_0 = Reg_2[0]; Reg_2_1 = Reg_2[1]; Reg_2_2 = Reg_2[2];
  //   Reg_2_3 = Reg_2[3]; Reg_2_4 = Reg_2[4]; Reg_3_0 = Reg_3[0]; Reg_3_1 = Reg_3[1]; Reg_3_2 = Reg_3[2];
  //   Reg_3_3 = Reg_3[3]; Reg_3_4 = Reg_3[4]; Reg_4_0 = Reg_4[0]; Reg_4_1 = Reg_4[1]; Reg_4_2 = Reg_4[2];
  //   Reg_4_3 = Reg_4[3]; Reg_4_4 = Reg_4[4]; Reg_5_0 = Reg_5[0]; Reg_5_1 = Reg_5[1]; Reg_5_2 = Reg_5[2];
  //   Reg_5_3 = Reg_5[3]; Reg_5_4 = Reg_5[4]; timer = out_18; Z_0_n = z_0; Z_1_n = z_1; Z_2_n = z_2

  // Notes on the sheet:
  //   PANNELLO CENTRALE ASCENSORE
  //   PANNELLO DI CONTROLLO RIPETIZIONE
  //   contents of rom_1 (hex, n*v repeats v):
  //   0,4,3,3,4*2,8*1
  //   contents of rom_2 (hex, n*v repeats v):
  //   0,1
  //   contents of rom_3 (hex, n*v repeats v):
  //   0,1
  //   contents of rom_4 (hex, n*v repeats v):
  //   0,1
  //   contents of rom_5 (hex, n*v repeats v):
  //   0,1
  //   contents of rom_6 (hex, n*v repeats v):
  //   0,1
  //   CONTROLLO 5
  //   COMPARATORE PANNELLO
  //   contents of rom_7 (hex, n*v repeats v):
  //   1,2,4,8,10
  //   contents of Registro_1 (hex, n*v repeats v):
  //   8*0,10,7*0,8,7*0,10,7*0,4,7*0,10,7*0,8,7*0,10,7*0,2,7*0,10,7*0
  //   ,8,7*0,10,7*0,4,7*0,10,7*0,8,7*0,10,7*0,1,7*0,10,7*0,8,7*0,10
  //   ,7*0,4,7*0,10,7*0,8,7*0,10,7*0,2,7*0,10,7*0,8,7*0,10,7*0,4,7*0
  //   ,10,7*0,8,7*0,10
  //   contents of Registro_2 (hex, n*v repeats v):
  //   9*0,10,7*0,8,6*0,8,10,7*0,4,6*0,4,10,6*0,4,8,6*0,8,10,7*0,2,6*0
  //   ,2,10,6*0,2,8,6*0,8,10,6*0,2,4,6*0,4,10,6*0,4,8,6*0,8,10,7*0,1
  //   ,6*0,1,10,6*0,1,8,6*0,8,10,6*0,1,4,6*0,4,10,6*0,4,8,6*0,8,10,6*0
  //   ,1,2,6*0,2,10,6*0,2,8,6*0,8,10,6*0,2,4,6*0,4,10,6*0,4,8,6*0,8
  //   contents of Registro_3 (hex, n*v repeats v):
  //   10*0,10,7*0,8,6*0,8,10,7*0,4,6*0,4,10,6*0,4,8,5*0,4,8,10,7*0,2
  //   ,6*0,2,10,6*0,2,8,5*0,2,8,10,6*0,2,4,5*0,2,4,10,5*0,2,4,8,5*0
  //   ,4,8,8*0,1,6*0,1,10,6*0,1,8,5*0,1,8,10,6*0,1,4,5*0,1,4,10,5*0
  //   ,1,4,8,5*0,4,8,7*0,1,2,5*0,1,2,10,5*0,1,2,8,5*0,2,8,6*0,1,2,4
  //   ,5*0,2,4,6*0,2,4,6*0,4
  //   contents of Registro_4 (hex, n*v repeats v):
  //   11*0,10,7*0,8,6*0,8,10,7*0,4,6*0,4,10,6*0,4,8,5*0,4,8,8*0,2,6*0
  //   ,2,10,6*0,2,8,5*0,2,8,7*0,2,4,5*0,2,4,6*0,2,4,5*0,2,4,9*0,1,6*0
  //   ,1,10,6*0,1,8,5*0,1,8,7*0,1,4,5*0,1,4,6*0,1,4,5*0,1,4,8*0,1,2
  //   ,5*0,1,2,6*0,1,2,5*0,1,2,7*0,1,2,5*0,1,2,6*0,1,2,6*0,2
  //   contents of Registro_5 (hex, n*v repeats v):
  //   12*0,10,7*0,8,6*0,8,8*0,4,6*0,4,7*0,4,6*0,4,9*0,2,6*0,2,7*0,2
  //   ,6*0,2,8*0,2,6*0,2,7*0,2,6*0,1,10*0,1,6*0,1,7*0,1,6*0,1,8*0,1
  //   ,6*0,1,7*0,1,6*0,1,9*0,1,6*0,1,7*0,1,6*0,1,8*0,1,6*0,1,7*0,1,6*0,1
  //   PULSANTI CHIAMATA PIANO
  //   TEMPO DI ATTESA
  //   Arrivo al piano
  //   contents of rom_8 (hex, n*v repeats v):
  //   3e9,9,0,9,0,9,0,9,6*0,9,0,16*a,16*0,a,0,a,0,a,0,a,0,a,0,a,0,a
  //   ,0,a,12*0,9
  //   contents of rom_9 (hex, n*v repeats v):
  //   9,9,0,9,0,9,0,9,0,9,9,9,0,9,9,9,0,9,0,9,9,9,0,9,0,9,0,9,0,9,9,9
  //   ,2,0,2,0,2,0,2,0,2,0,2,0,2,0,2,0,2,0,2,0,2,0,2,0,2,0,2,0,2,0,2
  //   ,33*0,2,0,2,0,2,0,2,0,2,0,2,0,2,0,2,0,2,0,2,0,2,0,2,0,2,0,2,0
  //   ,2,0,2
  //   contents of rom_10 (hex, n*v repeats v):
  //   9,9,0,9,0,9,0,9,0,9,9,9,0,9,9,9,0,9,0,9,9,9,0,9,0,9,0,9,0,9,9,9
  //   ,2,0,2,0,2,0,2,0,2,0,2,0,2,0,2,0,2,0,2,0,2,0,2,0,2,0,2,0,2,0,2
  //   ,33*0,2,0,2,0,2,0,2,0,2,0,2,0,2,0,2,0,2,0,2,0,2,0,2,0,2,0,2,0
  //   ,2,0,2
  //   contents of rom_11 (hex, n*v repeats v):
  //   9,9,0,9,0,9,0,9,0,9,9,9,0,9,9,9,0,9,0,9,9,9,0,9,0,9,0,9,0,9,9,9
  //   ,2,0,2,0,2,0,2,0,2,0,2,0,2,0,2,0,2,0,2,0,2,0,2,0,2,0,2,0,2,0,2
  //   ,33*0,2,0,2,0,2,0,2,0,2,0,2,0,2,0,2,0,2,0,2,0,2,0,2,0,2,0,2,0
  //   ,2,0,2
  //   PANNELLO PIANO LIBERO
  //   contents of rom_12 (hex, n*v repeats v):
  //   0,0,0,3,3,0,0,0,3,4,4,3,b,0,0,0,1,1,0,3,b,11*0,1,1,0,3,b,27*0
  //   ,1,1,0,3,b,59*0,1,1,0,3,b,126*0,3,3,0,0,0,2,0,2,3,b,0,0,0,3,4,4
  //   ,3,b,11*0,1,1,0,3,b,27*0,1,1,0,3,b,59*0,1,1,0,3,b,126*0,3,3,0,0,0
  //   ,2,0,2,3,b,0,0,0,2,0,2,3,b,11*0,3,4,4,3,b,27*0,1,1,0,3,b,59*0
  //   ,1,1,0,3,b,126*0,3,3,0,0,0,2,0,2,3,b,0,0,0,2,0,2,3,b,11*0,2,0
  //   ,2,3,b,27*0,3,4,4,3,b,59*0,1,1,0,3,b,126*0,3,3,0,0,0,2,0,2,3,b
  //   ,0,0,0,2,0,2,3,b,11*0,2,0,2,3,b,27*0,2,0,2,3,b,59*0,3,4,4,3,b
  //   ,910*0,1,15*0,1,31*0,1,63*0,1,135*0,2,23*0,1,31*0,1,63*0,1,135*0
  //   ,2,7*0,2,47*0,1,63*0,1,135*0,2,7*0,2,15*0,2,95*0,1,135*0,2,7*0
  //   ,2,15*0,2,31*0,2
  //   contents of rom_13 (hex, n*v repeats v):
  //   4*0,1,123*0,5*1
  //   contents of rom_14 (hex, n*v repeats v):
  //   0,0,1,1,28*0,5*1,27*0,5*1
  //   contents of rom_15 (hex, n*v repeats v):
  //   0,1,0,1,12*0,5*1,43*0,5*1
  //   PULSANTI DI CHIAMATA
  //   Stato ascensore
  //   Piano corrente
  //   TEST E TEMPO CLOCK
endmodule

/* Test case porte:
CK P_0 P_1 P_2 P_3 P_VIP A_0 A_1 A_2 A_3 A_VIP y_2 y_1 y_0 z_2 z_1 z_0
0  1   0   0   0   0     0   0   0   0   0     0   0   0   0   0   0  
C  0   0   0   0   0     0   0   0   0   0     0   0   0   0   1   1  
C  0   0   0   0   0     0   0   0   0   0     0   0   0   0   1   1  
C  0   0   0   0   0     0   0   0   0   0     0   0   0   0   1   1  
C  0   0   0   0   0     0   0   0   0   0     0   0   0   0   1   1  
C  0   0   0   0   0     0   0   0   0   0     0   0   0   0   1   1  
C  0   0   0   0   0     0   0   0   0   0     0   0   0   0   1   1  
C  0   0   0   0   0     0   0   0   0   0     0   0   0   0   1   1  
C  0   0   0   0   0     0   0   0   0   0     0   0   0   0   1   1  
C  0   0   0   0   0     0   0   0   0   0     0   0   0   0   1   1  
C  0   0   0   0   0     0   0   0   0   0     0   0   0   0   0   0  
*/

/* Test case piani:
CK P_0 P_1 P_2 P_3 P_VIP A_0 A_1 A_2 A_3 A_VIP y_2 y_1 y_0 z_2 z_1 z_0
0  0   1   1   1   0     0   0   0   0   0     0   0   0   0   0   0
C  0   0   0   0   0     0   0   0   0   0     0   0   0   0   0   1
0  0   0   0   0   0     0   1   0   0   0     0   0   0   0   0   1
1  0   0   0   0   0     0   1   0   0   0     0   0   1   1   0   0
C  0   0   0   0   0     0   0   0   0   0     0   0   1   1   0   0  
C  0   0   0   0   0     0   0   0   0   0     0   0   1   0   1   1  
C  0   0   0   0   0     0   0   0   0   0     0   0   1   0   1   1  
C  0   0   0   0   0     0   0   0   0   0     0   0   1   0   1   1  
C  0   0   0   0   0     0   0   0   0   0     0   0   1   0   1   1  
C  0   0   0   0   0     0   0   0   0   0     0   0   1   0   1   1  
C  0   0   0   0   0     0   0   0   0   0     0   0   1   0   1   1  
C  0   0   0   0   0     0   0   0   0   0     0   0   1   0   1   1  
C  0   0   0   0   0     0   0   0   0   0     0   0   1   0   1   1  
C  0   0   0   0   0     0   0   0   0   0     0   0   1   0   1   1  
C  0   0   0   0   0     0   0   0   0   0     0   0   1   0   0   1 
C  0   0   0   0   0     0   0   0   0   0     0   0   1   0   0   1
0  0   0   0   0   0     0   0   1   0   0     0   0   1   0   0   1
1  0   0   0   0   0     0   0   1   0   0     0   1   0   1   0   0
C  0   0   0   0   0     0   0   0   0   0     0   1   0   1   0   0  
C  0   0   0   0   0     0   0   0   0   0     0   1   0   0   1   1  
C  0   0   0   0   0     0   0   0   0   0     0   1   0   0   1   1  
C  0   0   0   0   0     0   0   0   0   0     0   1   0   0   1   1  
C  0   0   0   0   0     0   0   0   0   0     0   1   0   0   1   1  
C  0   0   0   0   0     0   0   0   0   0     0   1   0   0   1   1  
C  0   0   0   0   0     0   0   0   0   0     0   1   0   0   1   1  
C  0   0   0   0   0     0   0   0   0   0     0   1   0   0   1   1  
C  0   0   0   0   0     0   0   0   0   0     0   1   0   0   1   1  
C  0   0   0   0   0     0   0   0   0   0     0   1   0   0   1   1  
C  0   0   0   0   0     0   0   0   0   0     0   1   0   0   0   1 
C  0   0   0   0   0     0   0   0   0   0     0   1   0   0   0   1
0  0   0   0   0   0     0   0   0   1   0     0   1   0   0   0   1
1  0   0   0   0   0     0   0   0   1   0     0   1   1   1   0   0
C  0   0   0   0   0     0   0   0   0   0     0   1   1   1   0   0  
C  0   0   0   0   0     0   0   0   0   0     0   1   1   0   1   1  
C  0   0   0   0   0     0   0   0   0   0     0   1   1   0   1   1  
C  0   0   0   0   0     0   0   0   0   0     0   1   1   0   1   1  
C  0   0   0   0   0     0   0   0   0   0     0   1   1   0   1   1  
C  0   0   0   0   0     0   0   0   0   0     0   1   1   0   1   1  
C  0   0   0   0   0     0   0   0   0   0     0   1   1   0   1   1  
C  0   0   0   0   0     0   0   0   0   0     0   1   1   0   1   1  
C  0   0   0   0   0     0   0   0   0   0     0   1   1   0   1   1  
C  0   0   0   0   0     0   0   0   0   0     0   1   1   0   1   1  
C  0   0   0   0   0     0   0   0   0   0     0   1   1   0   0   0 
C  0   0   0   0   1     0   0   0   0   0     0   1   1   0   0   1
0  0   0   0   0   0     0   0   0   0   1     0   1   1   0   0   1
1  0   0   0   0   0     0   0   0   0   1     1   0   0   1   0   0
C  0   0   0   0   0     0   0   0   0   0     1   0   0   1   0   0  
C  0   0   0   0   0     0   0   0   0   0     1   0   0   0   1   1  
C  0   0   0   0   0     0   0   0   0   0     1   0   0   0   1   1  
C  0   0   0   0   0     0   0   0   0   0     1   0   0   0   1   1  
C  0   0   0   0   0     0   0   0   0   0     1   0   0   0   1   1  
C  0   0   0   0   0     0   0   0   0   0     1   0   0   0   1   1  
C  0   0   0   0   0     0   0   0   0   0     1   0   0   0   1   1  
C  0   0   0   0   0     0   0   0   0   0     1   0   0   0   1   1  
C  0   0   0   0   0     0   0   0   0   0     1   0   0   0   1   1  
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*/

/* Test case VIP:
CK P_0 P_1 P_2 P_3 P_VIP A_0 A_1 A_2 A_3 A_VIP y_2 y_1 y_0 z_2 z_1 z_0
0  0   1   1   1   1     0   0   0   0   0     0   0   0   0   0   0
C  0   0   0   0   0     0   0   0   0   0     0   0   0   0   0   1
0  0   0   0   0   0     0   1   0   0   0     0   0   0   0   0   1
1  0   0   0   0   0     0   1   0   0   0     0   0   1   0   0   1
C  0   0   0   0   0     0   0   0   0   0     0   0   1   0   0   1
0  0   0   0   0   0     0   0   1   0   0     0   0   1   0   0   1
1  0   0   0   0   0     0   0   1   0   0     0   1   0   0   0   1
C  0   0   0   0   0     0   0   0   0   0     0   1   0   0   0   1
0  0   0   0   0   0     0   0   0   1   0     0   1   0   0   0   1
1  0   0   0   0   0     0   0   0   1   0     0   1   1   0   0   1
C  0   0   0   0   0     0   0   0   0   0     0   1   1   0   0   1
0  0   0   0   0   0     0   0   0   0   1     0   1   1   0   0   1
1  0   0   0   0   0     0   0   0   0   1     1   0   0   1   0   0
C  0   0   0   0   0     0   0   0   0   0     1   0   0   1   0   0
C  0   0   0   0   0     0   0   0   0   0     1   0   0   0   1   1  
C  0   0   0   0   0     0   0   0   0   0     1   0   0   0   1   1  
C  0   0   0   0   0     0   0   0   0   0     1   0   0   0   1   1  
C  0   0   0   0   0     0   0   0   0   0     1   0   0   0   1   1  
C  0   0   0   0   0     0   0   0   0   0     1   0   0   0   1   1  
C  0   0   0   0   0     0   0   0   0   0     1   0   0   0   1   1  
C  0   0   0   0   0     0   0   0   0   0     1   0   0   0   1   1  
C  0   0   0   0   0     0   0   0   0   0     1   0   0   0   1   1  
C  0   0   0   0   0     0   0   0   0   0     1   0   0   0   1   1  
C  0   0   0   0   0     0   0   0   0   0     1   0   0   0   1   0  
0  0   0   0   0   0     0   0   0   1   0     1   0   0   0   1   0
1  0   0   0   0   0     0   0   0   1   0     0   1   1   1   0   0
C  0   0   0   0   0     0   0   0   0   0     0   1   1   1   0   0  
C  0   0   0   0   0     0   0   0   0   0     0   1   1   0   1   1  
C  0   0   0   0   0     0   0   0   0   0     0   1   1   0   1   1  
C  0   0   0   0   0     0   0   0   0   0     0   1   1   0   1   1  
C  0   0   0   0   1     0   0   0   0   0     0   1   1   0   1   1  
C  0   0   0   0   0     0   0   0   0   0     0   1   1   0   1   1  
C  0   0   0   0   0     0   0   0   0   0     0   1   1   0   1   1  
C  0   0   0   0   0     0   0   0   0   0     0   1   1   0   1   1  
C  0   0   0   0   0     0   0   0   0   0     0   1   1   0   1   1  
C  0   0   0   0   0     0   0   0   0   0     0   1   1   0   1   1  
C  0   0   0   0   0     0   0   0   0   0     0   1   1   0   0   1  
0  0   0   0   0   0     0   0   0   0   1     0   1   1   0   0   1
1  0   0   0   0   0     0   0   0   0   1     1   0   0   1   0   0
C  0   0   0   0   0     0   0   0   0   0     1   0   0   1   0   0
C  0   0   0   0   0     0   0   0   0   0     1   0   0   0   1   1  
C  0   0   0   0   0     0   0   0   0   0     1   0   0   0   1   1  
C  0   0   0   0   0     0   0   0   0   0     1   0   0   0   1   1  
C  0   0   0   0   0     0   0   0   0   0     1   0   0   0   1   1  
C  0   0   0   0   0     0   0   0   0   0     1   0   0   0   1   1  
C  0   0   0   0   0     0   0   0   0   0     1   0   0   0   1   1  
C  0   0   0   0   0     0   0   0   0   0     1   0   0   0   1   1  
C  0   0   0   0   0     0   0   0   0   0     1   0   0   0   1   1  
C  0   0   0   0   0     0   0   0   0   0     1   0   0   0   1   1  
C  0   0   0   0   0     0   0   0   0   0     1   0   0   0   1   0  
*/
