// Digital circuit String Recognizer - Circuit.dig as structural Verilog
module String_Recognizer___Circuit (
  input  x_1,
  input  x_0,
  input  CK,
  output z
);

  wire rom_1_d, rom_2_d, rom_3_d;
  wire [4:2] d_ff_1_q;

  ROM #(.AddrBits(5)) rom_1 (.A({d_ff_1_q, x_1, x_0}), .sel(1'b1), .D(rom_1_d));
  ROM #(.AddrBits(5)) rom_2 (.A({d_ff_1_q, x_1, x_0}), .sel(1'b1), .D(rom_2_d));
  ROM #(.AddrBits(5)) rom_3 (.A({d_ff_1_q, x_1, x_0}), .sel(1'b1), .D(rom_3_d));
  ROM #(.AddrBits(5)) rom_4 (.A({d_ff_1_q, x_1, x_0}), .sel(1'b1), .D(z));
  D_FF d_ff_1 (.D(rom_1_d), .C(CK), .Q(d_ff_1_q[2]));  // open: nQ
  D_FF d_ff_2 (.D(rom_2_d), .C(CK), .Q(d_ff_1_q[3]));  // open: nQ
  D_FF d_ff_3 (.D(rom_3_d), .C(CK), .Q(d_ff_1_q[4]));  // open: nQ

  // Notes on the sheet:
  //   contents of rom_1 (hex, n*v repeats v):
  //   0,1,0,0,0,1,0,0,0,1,1,0,0,1,0,0,0,1,1,0,0,1,0,0,0,1,1
  //   contents of rom_2 (hex, n*v repeats v):
  //   4*0,1,5*0,1,7*0,1,0,1,5*0,1
  //   contents of rom_3 (hex, n*v repeats v):
  //   9*0,1,5*0,1,0,1,0,0,1,4*0,1
  //   contents of rom_4 (hex, n*v repeats v):
  //   27*1,0,4*1
endmodule
